# Fritzing sketch circuit_diagram (saved by Fritzing 0.9.5d)

parts:
  Part1 = Arduino Uno (Rev3)
  S1 = H-Bridge with L298N
  Part2 = Bluetooth HC-05 Macho
  M1 = DC Motor
  M2 = DC Motor
  M3 = DC Motor
  M4 = DC Motor
  BAT2 = 12 battery [package=battery]
  S2 = Toggle Switch [package=THT]

nets:
  N1: Part1.D10_PWM/SS, Part2.TXD
  N2: Part1.D11_PWM/MOSI, Part2.RXD
  N3: Part1.D2, S1.IN1
  N4: Part1.D3_PWM, S1.IN2
  N5: Part1.D4, S1.IN3
  N6: Part1.D5_PWM, S1.IN4
  5V: Part1.5V, Part2.VCC
  GND: Part1.GND, S1.GND, Part2.GND, BAT2.-
  VIN: Part1.VIN, S1.12V, S2.L1
  N7: S1.ENA, S1.ENA-5V
  N8: S1.ENB, S1.ENB-5V
  N9: S1.M1-01, M1.pin_2, M2.pin_2
  N10: S1.M1-02, M1.pin_1, M2.pin_1
  N11: S1.M2-01, M3.pin_1, M4.pin_1
  N12: S1.M2-02, M3.pin_2, M4.pin_2
  N13: BAT2.+, S2.L2

custom parts:
  H-Bridge with L298N: h-bridge
  12 battery: 12V lead acid type battery, like the Husqvarna YTH2448 12V 35AH battery. This is the mini version 1/4 the size of the actual battery to be closer to typical breadboard parts (around 2in wide rathher than 7in). The pads in pcb are sized to accomidate up to 14ga wire (as these batterys will deliver high currents.)
